# Fritzing sketch Wiring (saved by Fritzing 0.9.4)
breadboards: 1

parts:
  Bauteil1 = Arduino Uno (Rev3)
  Bauteil2 = Arduino Nano (Rev3.0)
  C2 = Electrolytic Capacitor [capacitance=10µF package="100 mil [THT, electrolytic]"]

nets:
  N1: Bauteil1.D10_PWM/SS, Bauteil2.RESET, C2.-
  N2: Bauteil1.D11_PWM/MOSI, Bauteil2.D11/MOSI
  N3: Bauteil1.D12/MISO, Bauteil2.D12/MISO
  N4: Bauteil1.D13/SCK, Bauteil2.D13/SCK
  5V: Bauteil1.5V, Bauteil2.5V
  GND: Bauteil1.GND, Bauteil2.GND, C2.+

notes:
  Arduino Uno (Programmer)
  Arduino Nano (Target)
