# Fritzing sketch Wiring_nanos_only (saved by Fritzing 0.9.3b)
breadboards: 1

parts:
  Bauteil2 = Arduino Nano (Rev3.0)
  C2 = Electrolytic Capacitor [capacitance=10µF package="100 mil [THT, electrolytic]"]
  Bauteil3 = Arduino Nano (Rev3.0)

nets:
  N1: Bauteil2.RESET, C2.-, Bauteil3.RESET
  N2: Bauteil2.D11/MOSI, Bauteil3.D11/MOSI
  N3: Bauteil2.D12/MISO, Bauteil3.D12/MISO
  GND: Bauteil2.GND, C2.+, Bauteil3.GND
  5V: Bauteil2.5V, Bauteil3.5V
  N4: Bauteil2.D13/SCK, Bauteil3.D13/SCK

notes:
  Arduino Nano (Programmer)
  Arduino Nano (Target)
