# Fritzing sketch HowTo_Fritzing_Part-1 (saved by Fritzing 0.9.4)
breadboards: 1

parts:
  Bauteil1 = Arduino Uno (Rev3)
  LED1 = LED - 5mm [color="Red (633nm)" package="5 mm [THT]"]
  Bauteil2 = BME280 Breakout
  R1 = Resistor [tolerance=±5% resistance=220 package=THT]

nets:
  N1: Bauteil1.D12/MISO, Bauteil2.SDI/SDA
  N2: Bauteil1.D13/SCK, Bauteil2.SCK/SCL
  N3: Bauteil1.D0/RX, R1.Pin_0
  3V3: Bauteil1.3V3, Bauteil2.3.3V
  GND: Bauteil1.GND, LED1.cathode, Bauteil2.GND
  N4: LED1.anode, R1.Pin_1
