# Fritzing sketch HowTo_Fritzing_Part-2 (saved by Fritzing 0.9.4)
breadboards: 1

parts:
  Arduino_Uno_(Rev3) = Arduino Uno (Rev3)
  LED_(rot) = LED - 5mm [color="Red (633nm)" package="5 mm [THT]"]
  BME280_(Temperatursensor) = BME280 Breakout
  Widerstand_(R1) = Resistor [tolerance=±5% resistance=220 package=THT]

nets:
  N1: Arduino_Uno_(Rev3).D12/MISO, BME280_(Temperatursensor).SDI/SDA
  N2: Arduino_Uno_(Rev3).D13/SCK, BME280_(Temperatursensor).SCK/SCL
  N3: Arduino_Uno_(Rev3).D0/RX, Widerstand_(R1).Pin_0
  3V3: Arduino_Uno_(Rev3).3V3, BME280_(Temperatursensor).3.3V
  GND: Arduino_Uno_(Rev3).GND, LED_(rot).cathode, BME280_(Temperatursensor).GND
  N4: LED_(rot).anode, Widerstand_(R1).Pin_1
