# Fritzing sketch ESP_example1 (saved by Fritzing 0.9.4)
breadboards: 1

parts:
  U1 = ESP32-38PinWide [part_number=ESP32-38PinWide]
  S1 = Pushbutton [package="[THT]"]

nets:
  N1: U1.GPIO0, S1.Pin_1, S1.Pin_2
  N2: U1.GND, S1.Pin_3, S1.Pin_4

custom parts:
  ESP32-38PinWide: Generic 38-Pin ESP32 with wide format (only access to one side of pins on a breadboard) based on Stephen Lilley's HiLetgo ESP-WROOM-32 ESP32 ESP-32S Development Board.
