# Fritzing sketch Heartbeat_wiring_example_2 (saved by Fritzing 0.9.4)

parts:
  U1 = ESP32-38PinWide [part_number=ESP32-38PinWide]
  Bauteil1 = Arduino Uno (Rev3)

nets:
  N1: U1.EN, Bauteil1.D13/SCK
  N2: U1.GPIO27, Bauteil1.D3_PWM
  N3: U1.GPIO14, Bauteil1.D2
  GND: U1.GND, Bauteil1.GND
  VIN: U1.VIN, Bauteil1.5V

notes:
  Master
  Slave

custom parts:
  ESP32-38PinWide: Generic 38-Pin ESP32 with wide format (only access to one side of pins on a breadboard) based on Stephen Lilley's HiLetgo ESP-WROOM-32 ESP32 ESP-32S Development Board.
