# Fritzing sketch Wiring (saved by Fritzing 0.9.4)
breadboards: 1

parts:
  R1 = Resistor [tolerance=±5% resistance=220 package=THT]
  Bauteil1 = Arduino Ethernet Shield (Rev3)
  LED1 = LED - 5mm [color="Red (633nm)" package="5 mm [THT]"]
  Bauteil2 = LCD1602-I2C

nets:
  N1: R1.Pin_0, LED1.cathode
  GND: R1.Pin_1, Bauteil1.GND, Bauteil2.GND
  N2: Bauteil1.A4/SDA, Bauteil2.SDA
  N3: Bauteil1.A5/SCL, Bauteil2.SCL
  N4: Bauteil1.PWM_D6, LED1.anode
  5V: Bauteil1.5V, Bauteil2.VCC

notes:
  20x04 I2C-LCD-Display

custom parts:
  LCD1602-I2C: A standard character display, usually with 2x16 characters. Comes in many colors with LCM1602 IIC attached.
