# Fritzing sketch Wiring (saved by Fritzing 0.9.4)

parts:
  U1 = ESP8266 NodeMCU LoLin module
  R1 = Rotary Potentiometer (Small) [maximum_resistance=10kΩ package=THT]

nets:
  N1: U1.Vin, R1.leg1
  N2: U1.GND, R1.leg2
  N3: U1.A0, R1.wiper

custom parts:
  ESP8266 NodeMCU LoLin module: ESP8266 based NodeMCU
