# Fritzing sketch Weatherstation_old_update (saved by Fritzing 0.9.4)
circuit board: 8.46667cm x 5.64444cm
breadboards: 1

parts:
  OLED1 = OLED 128x64 I2C Monochrome Display
  U1 = ESP32-38PinWide [part_number=ESP32-38PinWide]

nets:
  GND: OLED1.GND, U1.GND
  N1: OLED1.VDD, U1.3.3
  N2: OLED1.SCK, U1.GPIO22
  N3: OLED1.SDA, U1.GPIO21

custom parts:
  ESP32-38PinWide: Generic 38-Pin ESP32 with wide format (only access to one side of pins on a breadboard) based on Stephen Lilley's HiLetgo ESP-WROOM-32 ESP32 ESP-32S Development Board.
