# Fritzing sketch Display_i2c (saved by Fritzing 0.9.4)

parts:
  Bauteil1 = Arduino Uno (Rev3)
  Bauteil2 = LCD1602-I2C

nets:
  N1: Bauteil1.A4/SDA, Bauteil2.SDA
  N2: Bauteil1.A5/SCL, Bauteil2.SCL
  5V: Bauteil1.5V, Bauteil2.VCC
  GND: Bauteil1.GND, Bauteil2.GND

custom parts:
  LCD1602-I2C: A standard character display, usually with 2x16 characters. Comes in many colors with LCM1602 IIC attached.
