# Fritzing sketch Display_oldschool (saved by Fritzing 0.9.4)
breadboards: 1

parts:
  LCD1 = LCD screen
  U1 = POT [package=pot_alpha_rv16af-20]
  Bauteil1 = Arduino Uno (Rev3)

nets:
  VSS: LCD1.VSS, LCD1.R/W, U1.A, Bauteil1.GND
  VDD: LCD1.VDD, U1.E, Bauteil1.5V
  N1: LCD1.V0, U1.S
  N2: LCD1.RS, Bauteil1.D12/MISO
  N3: LCD1.E, Bauteil1.D11_PWM/MOSI
  N4: LCD1.DB4, Bauteil1.D5_PWM
  N5: LCD1.DB5, Bauteil1.D4
  N6: LCD1.DB6, Bauteil1.D3_PWM
  N7: LCD1.DB7, Bauteil1.D2
