# Fritzing sketch Wiring (saved by Fritzing 0.9.4)
breadboards: 1

parts:
  Bauteil1 = BME/BMP280
  U1 = ESP32-38PinWide [part_number=ESP32-38PinWide]
  Bauteil2 = BME/BMP280

nets:
  VIN: Bauteil1.VIN, U1.3.3, Bauteil2.VIN
  GND: Bauteil1.GND, U1.GND, Bauteil2.GND
  N1: Bauteil1.SCL, U1.GPIO22
  N2: Bauteil1.SDA, U1.GPIO21
  N3: U1.GPIO16, Bauteil2.SCL
  N4: U1.GPIO17, Bauteil2.SDA

custom parts:
  BME/BMP280: Digital temperature humidity atmospheric pressure sensor
  ESP32-38PinWide: Generic 38-Pin ESP32 with wide format (only access to one side of pins on a breadboard) based on Stephen Lilley's HiLetgo ESP-WROOM-32 ESP32 ESP-32S Development Board.
